# Fritzing sketch BaboDuino - 1 (saved by Fritzing 0.8.3b)
circuit board: 6.88561cm x 5.36311cm
breadboards: 1

parts:
  S1 = Pushbutton [package="[THT]"]
  LED1 = LED - 3mm [color="Green (570nm)" package="3 mm [THT]"]
  R1 = Resistor [tolerance=±5% resistance=330 package=THT]
  R2 = Resistor [tolerance=±5% resistance=10k package=THT]
  U2 = Voltage Regulator - 5V [package="TO220 [THT]"]
  C2 = Electrolytic Capacitor [capacitance=10µF voltage=35V package="100 mil [THT, electrolytic]"]
  XTAL1 = Crystal [frequency="16 Mhz" package=THT]
  Power_plug1 = Power plug
  C5 = Electrolytic Capacitor [capacitance=10µF voltage=35V package="100 mil [THT, electrolytic]"]
  U1 = atmega328 [package=dip]
  C4 = Ceramic Capacitor [capacitance=22µF voltage=10V package="100 mil [THT, multilayer]"]
  C3 = Ceramic Capacitor [capacitance=22µF voltage=10V package="100 mil [THT, multilayer]"]
  J1 = female pin header, 6 pins [form="♀ (female)"]

nets:
  N1: S1.Pin_1, S1.Pin_2, R2.Pin_0, U1.RESET
  N2: S1.Pin_3, S1.Pin_4, LED1.cathode, U1.GND#7, C4.0, C3.1
  N3: LED1.anode, R1.Pin_1
  N4: R1.Pin_0, R2.Pin_1, U1.VCC
  N5: U2.input_voltage, Power_plug1.VCC, C5.+
  GND: U2.GND, C2.-, Power_plug1.GND, C5.-, U1.GND#21
  N6: U2.output_voltage, C2.+, U1.AVCC, U1.AREF
  N7: XTAL1.pin_0, U1.XLAT1, C4.1
  N8: XTAL1.pin_1, U1.XLAT2, C3.0
  N9: U1.A0, J1.pin6
  N10: U1.A1, J1.pin5
  N11: U1.A2, J1.pin4
  N12: U1.A3, J1.pin3
  N13: U1.A4, J1.pin2
  N14: U1.A5, J1.pin1
