# Fritzing sketch BaboDuino (saved by Fritzing 0.8.3b)
circuit board: 6.88561cm x 5.36311cm
breadboards: 1

parts:
  U2 = Voltage Regulator - 5V [package="TO220 [THT]"]
  C2 = Electrolytic Capacitor [capacitance=10µF voltage=35V package="100 mil [THT, electrolytic]"]
  Power_plug1 = Power plug
  C5 = Electrolytic Capacitor [capacitance=10µF voltage=35V package="100 mil [THT, electrolytic]"]
  U1 = atmega328 [package=dip]
  J1 = female pin header, 14 pins [form="♀ (female)"]
  J2 = female pin header, 4 pins [form="♀ (female)"]
  C3 = Ceramic Capacitor [capacitance=22µF voltage=10V package="100 mil [THT, multilayer]"]
  reset = Pushbutton [package="[THT]"]
  R2 = Resistor [tolerance=±5% resistance=10k package=THT]
  part = Resistor [tolerance=±5% resistance=330 package=THT]
  XTAL1 = Crystal [frequency="16 Mhz" package=THT]
  C4 = Ceramic Capacitor [capacitance=22µF voltage=10V package="100 mil [THT, multilayer]"]
  LED1 = LED - 3mm [color="Green (570nm)" package="3 mm [THT]"]

nets (from the schematic view):
  N1: U2.input_voltage, Power_plug1.VCC, C5.+
  GND: U2.GND, C2.-, Power_plug1.GND, C5.-, U1.GND#21, part.Pin_0
  N2: U2.output_voltage, C2.+, U1.AREF
  N3: U1.RESET, reset.Pin_1, reset.Pin_2, R2.Pin_0
  N4: U1.VCC, R2.Pin_1
  N5: U1.GND#7, U1.XLAT1, C3.1, reset.Pin_3, reset.Pin_4, XTAL1.pin_0, C4.0, C4.1, LED1.cathode
  N6: U1.XLAT2, C3.0, XTAL1.pin_1
  N7: U1.D5_(PWM), J2.pin1
  N8: U1.D6_(PWM), J2.pin2
  N9: U1.D7, J2.pin3
  N10: U1.D8, J2.pin4
  N11: U1.D9_(PWM), J1.pin14
  N12: U1.D10_(PWM), J1.pin13
  N13: U1.D11_(PWM), J1.pin12
  N14: U1.D12, J1.pin11
  N15: U1.D13, J1.pin10
  N16: U1.AVCC, J1.pin9
  N17: U1.A0, J1.pin6
  N18: U1.A1, J1.pin5
  N19: U1.A2, J1.pin4
  N20: U1.A3, J1.pin3
  N21: U1.A4, J1.pin2
  N22: U1.A5, J1.pin1

notes:
  Babo-duino
  v1.1
  A0
  A1
  A2
  A3
  A4
  A5
