# Fritzing sketch DIYDuino II (saved by Fritzing 0.8.3b)
circuit board: 5cm x 8cm
breadboards: 1

parts:
  U1 = atmega328 [package=dip]
  XTAL1 = Crystal [frequency="16 Mhz" package=THT]
  C1 = Ceramic Capacitor [capacitance=2.2µF package="100 mil [THT, multilayer]"]
  C2 = Ceramic Capacitor [capacitance=2.2µF package="100 mil [THT, multilayer]"]
  C4 = Electrolytic Capacitor [capacitance=10µF package="100 mil [THT, electrolytic]"]
  U2 = Voltage Regulator - 5V [package="TO220 [THT]"]
  R1 = Resistor [tolerance=±5% resistance=330 package=THT]
  R2 = Resistor [tolerance=±5% resistance=10k package=THT]
  Power_plug = Power plug
  reset = Pushbutton [package="[THT]"]
  A5 = rounded female pin header, 1 pin [form="♀ (female rounded)"]
  A0 = rounded female pin header, 1 pin [form="♀ (female rounded)"]
  A1 = rounded female pin header, 1 pin [form="♀ (female rounded)"]
  A2 = rounded female pin header, 1 pin [form="♀ (female rounded)"]
  A3 = rounded female pin header, 1 pin [form="♀ (female rounded)"]
  A4 = rounded female pin header, 1 pin [form="♀ (female rounded)"]
  D13 = rounded female pin header, 1 pin [form="♀ (female rounded)"]
  D12 = rounded female pin header, 1 pin [form="♀ (female rounded)"]
  D11 = rounded female pin header, 1 pin [form="♀ (female rounded)"]
  D10 = rounded female pin header, 1 pin [form="♀ (female rounded)"]
  D9 = rounded female pin header, 1 pin [form="♀ (female rounded)"]
  D8 = rounded female pin header, 1 pin [form="♀ (female rounded)"]
  D7 = rounded female pin header, 1 pin [form="♀ (female rounded)"]
  D6 = rounded female pin header, 1 pin [form="♀ (female rounded)"]
  D5 = rounded female pin header, 1 pin [form="♀ (female rounded)"]
  LED1 = LED - 3mm [color="Red (633nm)" package="3 mm [THT]"]
  RX/D0 = rounded female pin header, 1 pin [form="♀ (female rounded)"]
  TX/D1 = rounded female pin header, 1 pin [form="♀ (female rounded)"]
  D2 = rounded female pin header, 1 pin [form="♀ (female rounded)"]
  D3 = rounded female pin header, 1 pin [form="♀ (female rounded)"]
  D4 = rounded female pin header, 1 pin [form="♀ (female rounded)"]
  GND = female pin header, 10 pins [form="♀ (female)"]
  +5v = female pin header, 10 pins [form="♀ (female)"]
  1N4007 = Rectifier Diode [part_number=1N4007 package="300 mil [THT]"]
  C5 = Electrolytic Capacitor [package="100 mil [THT, electrolytic]"]

nets (from the pcb view):
  N1: U1.RESET, R2.Pin_0, reset.Pin_3, reset.Pin_4
  N2: U1.D0_(RX), RX/D0.pin1
  N3: U1.D1_(TX), TX/D1.pin1
  N4: U1.D2, D2.pin1
  N5: U1.D3_(PWM), D3.pin1
  N6: U1.D4, D4.pin1
  N7: U1.VCC, U1.AVCC, U1.AREF, C4.+, U2.output_voltage, R1.Pin_1, R2.Pin_1, +5v.pin1, +5v.pin2, +5v.pin3, +5v.pin4, +5v.pin5, +5v.pin6, +5v.pin7, +5v.pin8, +5v.pin9, +5v.pin10
  N8: U1.GND#7, C1.0, C2.0, reset.Pin_1, reset.Pin_2, LED1.anode, GND.pin1, GND.pin2, GND.pin3, GND.pin4, GND.pin5, GND.pin6, GND.pin7, GND.pin8, GND.pin9, GND.pin10
  N9: U1.XLAT1, XTAL1.pin_0, C2.1
  N10: U1.XLAT2, XTAL1.pin_1, C1.1
  N11: U1.D5_(PWM), D5.pin1
  N12: U1.D6_(PWM), D6.pin1
  N13: U1.D7, D7.pin1
  N14: U1.D8, D8.pin1
  N15: U1.D9_(PWM), D9.pin1
  N16: U1.D10_(PWM), D10.pin1
  N17: U1.D11_(PWM), D11.pin1
  N18: U1.D12, D12.pin1
  N19: U1.D13, D13.pin1
  GND: U1.GND#21, C4.-, U2.GND, Power_plug.GND, 1N4007.anode, C5.-
  N20: U1.A0, A0.pin1
  N21: U1.A1, A1.pin1
  N22: U1.A2, A2.pin1
  N23: U1.A3, A3.pin1
  N24: U1.A4, A4.pin1
  N25: U1.A5, A5.pin1
  N26: U2.input_voltage, Power_plug.VCC, 1N4007.cathode, C5.+
  N27: R1.Pin_0, LED1.cathode

notes:
  +5v
  Babo-duino
  v1.1
  GND

custom parts:
  Electrolytic Capacitor: A small electrolytic capacitor
